# Fritzing sketch gps_grid_sq_lcd (saved by Fritzing 0.9.3b)

parts:
  Part1 = Arduino Uno (Rev3)
  Part2 = LCD1602-I2C
  GY-NEO6MV3 = SUP500F [package=sup500f]

nets:
  N1: Part1.A4/SDA, Part2.SDA
  N2: Part1.A5/SCL, Part2.SCL
  N3: Part1.D2, GY-NEO6MV3.TX-O
  3V3: Part1.3V3, GY-NEO6MV3.VCC
  5V: Part1.5V, Part2.VCC
  GND: Part1.GND, Part2.GND, GY-NEO6MV3.GND

notes:
  GPS module
  3.3V
  TX data
  GND
  I2C 2x16 LCD char display
  5V
  GND
  SDA
  SCL
  +12VDC input -------->

custom parts:
  LCD1602-I2C: A standard character display, usually with 2x16 characters. Comes in many colors with LCM1602 IIC attached.
